// Logisim project Experiment 01.circ as structural Verilog: 1 circuit, main circuit main
module main (
  input  in_1,
  input  in_2,
  input  in_3,
  input  in_4,
  input  in_5,
  input  in_6,
  input  in_7,
  input  in_8,
  input  in_9,
  output out_10,
  output out_11,
  output out_12,
  output out_13,
  output out_14
);

  and and_1 (out_10, in_1, in_3);
  or or_1 (out_12, in_5, in_6);
  not not_1 (out_14, in_9);
  buf xor_1 (out_11, in_4);  // XOR_Gate
  not xnor_1 (out_13, in_7);  // XNOR_Gate
endmodule
