// Logisim project Experiment 12.circ as structural Verilog: 1 circuit, main circuit main
module main (
  input  in_1,
  input  in_2,
  input  in_3,
  input  in_4,
  input  [1:0] in_5,
  output out_6,
  output out_7,
  output out_8,
  output out_9,
  output out_10,
  output out_11,
  output out_12,
  output out_13
);

  wire not_1_out, not_2_out;

  Demultiplexer #(.select(2)) demultiplexer_1 (
    .out0(out_7), .out1(out_8), .out2(out_10), .out3(out_12), .in(in_4), .sel(in_5));  // open: en
  not not_1 (not_1_out, in_1);
  not not_2 (not_2_out, in_2);
  and and_1 (out_6, not_1_out, not_2_out, in_3);
  and and_2 (out_9, not_1_out, in_2, in_3);
  and and_3 (out_11, in_1, not_2_out, in_3);
  and and_4 (out_13, in_1, in_2, in_3);
endmodule
