// Logisim project experiment 03.circ as structural Verilog: 1 circuit, main circuit main
module main (
  input  in_1,
  input  in_2,
  input  in_3,
  input  in_4,
  input  in_5,
  output out_6,
  output out_7,
  output out_8
);

  wire nor_2_out, nor_3_out, nor_5_out;

  nor nor_1 (out_6, in_2, in_2);
  nor nor_2 (nor_2_out, in_4, in_4);
  not nor_3 (nor_3_out, in_5);  // NOR_Gate
  nor nor_4 (out_8, nor_2_out, nor_3_out);
  nor nor_5 (nor_5_out, in_1, in_3);
  nor nor_6 (out_7, nor_5_out, nor_5_out);
endmodule
